// Logisim project TN4.circ as structural Verilog: 1 circuit, main circuit TN4
module TN4 (
  input  A,
  input  B,
  input  C,
  input  D,
  output F_can,
  output EQ1,
  output F_sop,
  output EQ2,
  output F_pos
);

  wire and_1_out, and_2_out, and_3_out, and_4_out, and_5_out, and_6_out, and_7_out, and_8_out, and_9_out,
       and_10_out, and_11_out, and_12_out, and_13_out, and_14_out, and_15_out, and_16_out, and_17_out,
       and_18_out, and_19_out, and_20_out, and_21_out, and_22_out, and_23_out, and_24_out, and_25_out,
       and_26_out, and_27_out, not_1_out, not_2_out, not_3_out, not_4_out, not_5_out, not_6_out, not_7_out,
       not_8_out, not_9_out, not_10_out, not_11_out, not_12_out, not_13_out, not_14_out, not_15_out,
       not_16_out, not_17_out, not_18_out, not_19_out, not_20_out, not_21_out, not_22_out, not_23_out,
       not_24_out, not_25_out, not_26_out, not_27_out, not_28_out, not_29_out, not_30_out, not_31_out,
       not_32_out, not_33_out, not_34_out, not_35_out, not_36_out, not_37_out, not_38_out, not_39_out,
       not_40_out, not_41_out, not_42_out, not_43_out, not_44_out, not_45_out, not_46_out, not_47_out,
       not_48_out, not_49_out, not_50_out, or_1_out, or_2_out, or_3_out, or_4_out, or_5_out, or_7_out,
       or_8_out, or_9_out, or_10_out, or_11_out, or_13_out, or_14_out, or_15_out;

  not not_1 (not_1_out, A);
  not not_2 (not_2_out, B);
  not not_3 (not_3_out, D);
  not not_4 (not_4_out, A);
  not not_5 (not_5_out, B);
  not not_6 (not_6_out, A);
  not not_7 (not_7_out, C);
  not not_8 (not_8_out, A);
  not not_9 (not_9_out, B);
  not not_10 (not_10_out, C);
  not not_11 (not_11_out, A);
  not not_12 (not_12_out, B);
  not not_13 (not_13_out, D);
  not not_14 (not_14_out, A);
  not not_15 (not_15_out, B);
  not not_16 (not_16_out, A);
  not not_17 (not_17_out, C);
  not not_18 (not_18_out, A);
  not not_19 (not_19_out, B);
  not not_20 (not_20_out, C);
  not not_21 (not_21_out, A);
  not not_22 (not_22_out, B);
  not not_23 (not_23_out, A);
  not not_24 (not_24_out, C);
  not not_25 (not_25_out, B);
  not not_26 (not_26_out, A);
  and and_1 (and_1_out, not_26_out, not_27_out, C);
  not not_27 (not_27_out, B);
  not not_28 (not_28_out, A);
  and and_2 (and_2_out, not_28_out, B, D);
  and and_3 (and_3_out, B, not_29_out, D);
  not not_29 (not_29_out, C);
  not not_30 (not_30_out, B);
  and and_4 (and_4_out, not_30_out, C, D);
  not not_31 (not_31_out, A);
  not not_32 (not_32_out, B);
  not not_33 (not_33_out, D);
  not not_34 (not_34_out, A);
  not not_35 (not_35_out, B);
  not not_36 (not_36_out, A);
  not not_37 (not_37_out, C);
  not not_38 (not_38_out, A);
  not not_39 (not_39_out, B);
  not not_40 (not_40_out, C);
  not not_41 (not_41_out, B);
  not not_42 (not_42_out, A);
  not not_43 (not_43_out, A);
  not not_44 (not_44_out, B);
  not not_45 (not_45_out, C);
  or or_1 (or_1_out, B, C);
  or or_2 (or_2_out, C, D);
  not not_46 (not_46_out, B);
  or or_3 (or_3_out, not_46_out, C);
  not not_47 (not_47_out, A);
  or or_4 (or_4_out, not_47_out, B, D);
  not not_48 (not_48_out, A);
  not not_49 (not_49_out, B);
  or or_5 (or_5_out, not_48_out, not_49_out, not_50_out);
  not not_50 (not_50_out, C);
  and and_5 (and_5_out, not_4_out, not_5_out, C, D);
  and and_6 (and_6_out, not_6_out, B, not_7_out, D);
  and and_7 (and_7_out, not_8_out, B, C, D);
  and and_8 (and_8_out, A, C, D);
  and and_9 (and_9_out, A, not_10_out, D);
  and and_10 (and_10_out, not_11_out, not_12_out, C, not_13_out);
  and and_11 (and_11_out, not_14_out, not_15_out, C, D);
  and and_12 (and_12_out, not_16_out, not_17_out, D);
  and and_13 (and_13_out, not_18_out, B, C, D);
  and and_14 (and_14_out, A, not_19_out, C, D);
  and and_15 (and_15_out, A, B, not_20_out, D);
  and and_16 (and_16_out, not_21_out, not_22_out, C);
  and and_17 (and_17_out, not_23_out, B, D);
  and and_18 (and_18_out, B, not_24_out, D);
  and and_19 (and_19_out, not_25_out, C, D);
  or or_6 (F_sop, and_1_out, and_2_out, and_3_out, and_4_out);
  and and_20 (and_20_out, not_31_out, not_32_out, C, not_33_out);
  and and_21 (and_21_out, not_34_out, not_35_out, C, D);
  and and_22 (and_22_out, not_36_out, B, not_37_out, D);
  and and_23 (and_23_out, not_38_out, B, C, D);
  and and_24 (and_24_out, A, not_39_out, C, D);
  and and_25 (and_25_out, A, B, not_40_out, D);
  or or_7 (or_7_out, B, C);
  or or_8 (or_8_out, C, D);
  or or_9 (or_9_out, not_41_out, C);
  or or_10 (or_10_out, not_42_out, B, D);
  or or_11 (or_11_out, not_43_out, not_44_out, not_45_out);
  and and_26 (and_26_out, not_1_out, not_2_out, C, not_3_out);
  or or_12 (F_can, and_26_out, and_5_out, and_6_out, and_7_out, and_8_out, and_9_out);
  or or_13 (or_13_out, and_10_out, and_11_out, and_12_out, and_13_out, and_14_out, and_15_out);
  or or_14 (or_14_out, and_16_out, and_17_out, and_18_out, and_19_out);
  or or_15 (or_15_out, and_20_out, and_21_out, and_22_out, and_23_out, and_24_out, and_25_out);
  and and_27 (and_27_out, or_7_out, or_8_out, or_9_out, or_10_out, or_11_out);
  and and_28 (F_pos, or_1_out, or_2_out, or_3_out, or_4_out, or_5_out);
  xnor xnor_1 (EQ1, or_13_out, or_14_out);
  xnor xnor_2 (EQ2, or_15_out, and_27_out);
endmodule
