// Logisim project WARMUP.circ as structural Verilog
module WARMUP (
  input  A,
  input  B,
  output F
);

  wire not_1_out;

  not not_1 (not_1_out, B);
  and and_1 (F, A, not_1_out);
endmodule

module TN1 (
  input  A,
  input  B,
  input  C,
  output AND,
  output OR,
  output NAND,
  output NOR,
  output XOR,
  output CHAIN,
  output XNOR,
  output A_prime,
  output XOR3,
  output NAND3
);

  wire nand_1_out;

  nand nand_1 (nand_1_out, A, B);
  nand nand_2 (CHAIN, nand_1_out, C);
  not not_1 (A_prime, A);
  xor xor_1 (XOR3, A, B, C);
  nand nand_3 (NAND3, A, B, C);
  and and_1 (AND, A, B);
  or or_1 (OR, A, B);
  nand nand_4 (NAND, A, B);
  nor nor_1 (NOR, A, B);
  xor xor_2 (XOR, A, B);
  xnor xnor_1 (XNOR, A, B);
endmodule
