// Logisim project tn1.circ as structural Verilog: 1 circuit, main circuit TN1
module TN1 (
  input  A,
  input  B,
  input  C,
  output AND2,
  output A_INV,
  output OR2,
  output NAND2,
  output NOR2,
  output XOR2,
  output XNOR2,
  output XOR3,
  output NAND3,
  output CHAIN
);

  wire nand_3_out;

  not not_1 (A_INV, A);
  and and_1 (AND2, A, B);
  or or_1 (OR2, A, B);
  xor odd_parity_1 (XOR3, A, B, C);
  nand nand_1 (NAND2, A, B);
  nor nor_1 (NOR2, A, B);
  xor xor_1 (XOR2, A, B);
  xnor xnor_1 (XNOR2, A, B);
  nand nand_2 (NAND3, A, B, C);
  nand nand_3 (nand_3_out, A, B);
  nand nand_4 (CHAIN, nand_3_out, C);
endmodule
