// Logisim project tn3.circ as structural Verilog: 1 circuit, main circuit TN3
module TN3 (
  input  A,
  input  B,
  input  C,
  input  D,
  output F
);

  wire and_1_out, and_2_out, and_3_out, and_4_out, and_5_out, and_6_out, not_1_out, not_2_out, not_3_out,
       not_4_out, not_5_out, not_6_out, not_7_out, not_8_out, not_9_out, not_10_out;

  not not_1 (not_1_out, A);
  not not_2 (not_2_out, B);
  not not_3 (not_3_out, D);
  not not_4 (not_4_out, A);
  and and_1 (and_1_out, not_4_out, not_5_out, D);
  not not_5 (not_5_out, B);
  not not_6 (not_6_out, A);
  not not_7 (not_7_out, C);
  not not_8 (not_8_out, A);
  not not_9 (not_9_out, B);
  and and_2 (and_2_out, A, not_9_out, C, D);
  not not_10 (not_10_out, C);
  and and_3 (and_3_out, not_1_out, not_2_out, C, not_3_out);
  and and_4 (and_4_out, not_6_out, B, D);
  and and_5 (and_5_out, not_8_out, B, D);
  and and_6 (and_6_out, A, B, not_10_out, D);
  or or_1 (F, and_3_out, and_1_out, and_4_out, and_5_out, and_2_out, and_6_out);
endmodule
